# Fritzing sketch PAP (saved by Fritzing 0.9.3b)

parts:
  Power_plug1 = Power plug
  Часть1 = Arduino Pro Mini v13
  S1 = L298 Motor Driver
  ENCODER1 = Rotary Encoder Shield with Knob
  Часть2 = 4 Digit 7 Segment LED Display Shield
  M1 = DC Motor
  Часть3 = Hall Sensor Shield [part_number=DS18B20]

nets:
  GND: Power_plug1.GND, Часть1.GND, S1.GND, ENCODER1.GND, Часть2.GND, Часть3.GND
  N1: Power_plug1.VCC, S1.12V_IN
  VCC: Часть1.VCC, S1.5V_OUT, ENCODER1.VCC, Часть2.VCC, Часть3.VCC
  N2: Часть1.D11_PWM/MOSI, S1.ENA
  N3: Часть1.D10_PWM/SS, S1.IN2
  N4: Часть1.D9_PWM, S1.IN1
  N5: Часть1.D8, Часть2.SCLK
  N6: Часть1.D7, Часть2.RCLK
  N7: Часть1.D6_PWM, Часть2.DIO
  N8: Часть1.D5_PWM, ENCODER1.DT
  N9: Часть1.D4, ENCODER1.CLK
  N10: Часть1.D3_PWM, ENCODER1.SW
  N11: Часть1.D2, Часть3.S
  N12: S1.M1-01, M1.pin_2
  N13: S1.M1-02, M1.pin_1
